# Fritzing sketch fritzing_sketch (saved by Fritzing 0.9.3b)
circuit board: 10.0619cm x 6.01435cm

parts:
  RTC = Real Time Clock Module - DS1307 RTC Breakout Board
  Arduino = Arduino Nano (Rev3.0)
  JQ6500 = JQ6500
  SP1 = SPEAKER [package=pcb_mount_speaker]
  0_01_µF = Capacitor [package=cap-pth-small2]
  0_33_µF = Capacitor [package=cap-pth-small2]
  VCC1 = Battery block 9V
  S1 = SWITCH-MOMENTARY-2 [package=reed_switch_pth]
  U1 = Voltage Regulator - 5V [package="TO220 [THT]"]
  R1 = Resistor [tolerance=±5% resistance=1k package=THT]
  Keypad = KEYPAD 4x3

nets:
  5V: RTC.5V, Arduino.5V, JQ6500.VCC
  GND: RTC.GND, Arduino.GND, JQ6500.GND, 0_01_µF.2
  N1: RTC.SCL, Arduino.A5
  N2: RTC.SDA, Arduino.A4
  N3: Arduino.D2, JQ6500.TX
  N4: Arduino.D3, R1.Pin_0
  N5: Arduino.D7, Keypad.col1
  N6: Arduino.D8, Keypad.col2#26
  N7: Arduino.D9, Keypad.col2#27
  N8: Arduino.D10, Keypad.arrow2
  N9: Arduino.D11/MOSI, Keypad.col3
  N10: Arduino.D12/MISO, Keypad.arrow3
  N11: Arduino.D13/SCK, Keypad.arrow4
  N12: JQ6500.K2, JQ6500.K4
  N13: JQ6500.RX, R1.Pin_1
  N14: JQ6500.SPK-, SP1.-
  N15: JQ6500.SPK+, SP1.+
  N16: 0_33_µF.1, S1.2, U1.input_voltage
  N17: 0_33_µF.2, VCC1.-, U1.GND
  N18: VCC1.+, S1.1

notes:
  Audiokiste, 1.1

custom parts:
  KEYPAD 4x3: KEYPAD matricial de 12 botones, 4 filas x 3 columnas
